// Logisim project SubtractorFinal.circ as structural Verilog: 15 circuits, main circuit final_layout
// FA
module Full_Adder (
  input  A,
  input  B,
  input  C,
  output S,
  output C_2
);

  wire half_adder_1_c, half_adder_1_s, half_adder_2_c;

  Half_Adder half_adder_1 (.A(A), .B(B), .S(half_adder_1_s), .C(half_adder_1_c));
  Half_Adder half_adder_2 (.A(half_adder_1_s), .B(C), .S(S), .C(half_adder_2_c));
  or OR (C_2, half_adder_2_c, half_adder_1_c);
endmodule

// HA
module Half_Adder (
  input  A,
  input  B,
  output S,
  output C
);

  xor XOR (S, A, B);
  and AND (C, A, B);
endmodule

// Subtractor
module SubOrMult (
  input  B4,
  input  A4,
  input  B3,
  input  A3,
  input  B2,
  input  A2,
  input  B1,
  input  A1,
  input  B0,
  input  A0,
  input  M,
  output V,
  output C,
  output S4,
  output S3,
  output S2,
  output S1,
  output S0
);

  wire full_adder_2_c_2, full_adder_3_c_2, full_adder_4_c_2, full_adder_5_c_2, xor_2_out, xor_3_out,
       xor_4_out, xor_5_out, xor_6_out;

  xor xor_1 (V, C, full_adder_2_c_2);
  xor xor_2 (xor_2_out, B4, M);
  Full_Adder full_adder_1 (.A(A4), .B(xor_2_out), .C(full_adder_2_c_2), .S(S4), .C_2(C));
  xor xor_3 (xor_3_out, B3, M);
  Full_Adder full_adder_2 (.A(A3), .B(xor_3_out), .C(full_adder_3_c_2), .S(S3), .C_2(full_adder_2_c_2));
  xor xor_4 (xor_4_out, B2, M);
  Full_Adder full_adder_3 (.A(A2), .B(xor_4_out), .C(full_adder_4_c_2), .S(S2), .C_2(full_adder_3_c_2));
  xor xor_5 (xor_5_out, B1, M);
  Full_Adder full_adder_4 (.A(A1), .B(xor_5_out), .C(full_adder_5_c_2), .S(S1), .C_2(full_adder_4_c_2));
  xor xor_6 (xor_6_out, B0, M);
  Full_Adder full_adder_5 (.A(A0), .B(xor_6_out), .C(M), .S(S0), .C_2(full_adder_5_c_2));

  // Notes on the sheet:
  //   Detect Over Flow
  //   16
  //   If 1 then Positive
  //   8
  //   4
  //   2
  //   1
endmodule

module _2_s_Compliment (
  input  S0,
  input  S1,
  input  S2,
  input  S3,
  input  S4,
  input  _111,
  output [4:0] Out
);

  wire half_adder_1_c, half_adder_2_c, half_adder_3_c, half_adder_4_c, not_1_out, not_2_out, not_3_out,
       not_4_out, not_5_out;

  not not_1 (not_1_out, S0);
  not not_2 (not_2_out, S1);
  not not_3 (not_3_out, S2);
  not not_4 (not_4_out, S3);
  not not_5 (not_5_out, S4);
  Half_Adder half_adder_1 (.A(not_1_out), .B(_111), .S(Out[0]), .C(half_adder_1_c));
  Half_Adder half_adder_2 (.A(not_2_out), .B(half_adder_1_c), .S(Out[1]), .C(half_adder_2_c));
  Half_Adder half_adder_3 (.A(not_3_out), .B(half_adder_2_c), .S(Out[2]), .C(half_adder_3_c));
  Half_Adder half_adder_4 (.A(not_4_out), .B(half_adder_3_c), .S(Out[3]), .C(half_adder_4_c));
  Half_Adder half_adder_5 (.A(not_5_out), .B(half_adder_4_c), .S(Out[4]));  // open: C
endmodule

module _0 (
  input  a,
  input  b,
  input  c,
  input  d,
  output z
);

  wire and_1_out, and_2_out, not_1_out, not_2_out;

  not not_1 (not_1_out, b);
  not not_2 (not_2_out, d);
  and and_1 (and_1_out, not_1_out, not_2_out);
  and and_2 (and_2_out, b, d);
  or or_1 (z, and_1_out, c, and_2_out, a);
endmodule

module _1 (
  input  a,
  input  b,
  input  c,
  input  d,
  output z
);

  wire not_1_out, not_2_out, not_3_out;

  not not_1 (not_1_out, a);
  not not_2 (not_2_out, b);
  not not_3 (not_3_out, c);
  and and_1 (z, not_1_out, not_2_out, not_3_out, d);
endmodule

module _4_bit_decoder___7_display (
  input  D,
  input  C,
  input  B,
  input  A,
  output a_2,
  output b_2,
  output c_2,
  output d_2,
  output e,
  output f,
  output g
);

  wire and_1_out, and_2_out, and_3_out, and_4_out, and_5_out, and_6_out, and_7_out, and_8_out, and_9_out,
       and_10_out, and_11_out, and_12_out, and_13_out, and_14_out, and_15_out, and_16_out, not_1_out,
       not_2_out, not_3_out, not_4_out, not_5_out, not_6_out, not_7_out, not_8_out, not_9_out, not_10_out,
       not_11_out, not_12_out, not_13_out, not_14_out, not_15_out, not_16_out, not_17_out, not_18_out,
       not_19_out, not_20_out, not_21_out;

  not not_1 (not_1_out, D);
  and and_1 (and_1_out, not_1_out, not_2_out);
  not not_2 (not_2_out, B);
  and and_2 (and_2_out, D, B);
  not not_3 (not_3_out, D);
  and and_3 (and_3_out, not_3_out, not_4_out);
  not not_4 (not_4_out, C);
  not not_5 (not_5_out, B);
  and and_4 (and_4_out, D, C);
  not not_6 (not_6_out, C);
  or or_1 (c_2, not_6_out, B, D);
  not not_7 (not_7_out, D);
  and and_5 (and_5_out, not_7_out, not_8_out);
  not not_8 (not_8_out, B);
  not not_9 (not_9_out, D);
  and and_6 (and_6_out, not_9_out, C);
  and and_7 (and_7_out, C, not_10_out);
  not not_10 (not_10_out, B);
  not not_11 (not_11_out, C);
  and and_8 (and_8_out, D, not_11_out, B);
  not not_12 (not_12_out, D);
  and and_9 (and_9_out, not_12_out, not_13_out);
  not not_13 (not_13_out, B);
  not not_14 (not_14_out, D);
  and and_10 (and_10_out, not_14_out, C);
  not not_15 (not_15_out, D);
  and and_11 (and_11_out, not_15_out, not_16_out);
  not not_16 (not_16_out, C);
  not not_17 (not_17_out, D);
  and and_12 (and_12_out, not_17_out, B);
  not not_18 (not_18_out, C);
  and and_13 (and_13_out, not_18_out, B);
  not not_19 (not_19_out, C);
  and and_14 (and_14_out, not_19_out, B);
  not not_20 (not_20_out, D);
  and and_15 (and_15_out, not_20_out, C);
  and and_16 (and_16_out, C, not_21_out);
  not not_21 (not_21_out, B);
  or or_2 (a_2, and_1_out, A, C, and_2_out);
  or or_3 (b_2, and_3_out, not_5_out, and_4_out);
  or or_4 (d_2, and_5_out, A, and_6_out, and_7_out, and_8_out);
  or or_5 (e, and_9_out, and_10_out);
  or or_6 (f, and_11_out, A, and_12_out, and_13_out);
  or or_7 (g, A, and_14_out, and_15_out, and_16_out);
endmodule

module test_display (
  input  [3:0] in_1,
  input  [4:0] A,
  input  [4:0] in_3,
  input  [4:0] A_2,
  input  [4:0] A_3
);

  wire first_decoder_2_a, first_decoder_2_b, first_decoder_2_c, first_decoder_2_d, first_decoder_2_e,
       first_decoder_2_f, first_decoder_2_g, first_decoder_3_a, first_decoder_3_b, first_decoder_3_c,
       first_decoder_3_d, first_decoder_3_e, first_decoder_3_f, first_decoder_3_g, first_decoder_4_a,
       first_decoder_4_b, first_decoder_4_c, first_decoder_4_d, first_decoder_4_e, first_decoder_4_f,
       first_decoder_4_g, n4_bit_decoder_7_display_1_a_2, n4_bit_decoder_7_display_1_b_2,
       n4_bit_decoder_7_display_1_c_2, n4_bit_decoder_7_display_1_d_2, n4_bit_decoder_7_display_1_e,
       n4_bit_decoder_7_display_1_f, n4_bit_decoder_7_display_1_g, second_decoder_1_a, second_decoder_1_b,
       second_decoder_1_c, second_decoder_1_d, second_decoder_1_e, second_decoder_1_f, second_decoder_1_g,
       second_decoder_2_a, second_decoder_2_b, second_decoder_2_c, second_decoder_2_d, second_decoder_2_e,
       second_decoder_2_f, second_decoder_2_g, second_decoder_3_a, second_decoder_3_b, second_decoder_3_c,
       second_decoder_3_d, second_decoder_3_e, second_decoder_3_f, second_decoder_3_g;

  _4_bit_decoder___7_display u_4_bit_decoder_7_display_1 (
    .D(in_1[0]), .C(in_1[1]), .B(in_1[2]), .A(in_1[3]), .a_2(n4_bit_decoder_7_display_1_a_2),
    .b_2(n4_bit_decoder_7_display_1_b_2), .c_2(n4_bit_decoder_7_display_1_c_2),
    .d_2(n4_bit_decoder_7_display_1_d_2), .e(n4_bit_decoder_7_display_1_e), .f(n4_bit_decoder_7_display_1_f),
    .g(n4_bit_decoder_7_display_1_g));
  first_decoder first_decoder_1 (
    .C4(in_3[0]), .S3(in_3[1]), .S2(in_3[2]), .S1(in_3[3]), .S0(in_3[4]));  // open: a, b, c, d, e, f, g
  _7_Segment_Display u_7_segment_display_1 (
    .g(second_decoder_1_g), .f(second_decoder_1_f), .a(second_decoder_1_a), .b(second_decoder_1_b),
    .e(second_decoder_1_e), .d(second_decoder_1_d), .c(second_decoder_1_c));  // open: dp
  _7_Segment_Display u_7_segment_display_2 (
    .g(n4_bit_decoder_7_display_1_g), .f(n4_bit_decoder_7_display_1_f), .a(n4_bit_decoder_7_display_1_a_2),
    .b(n4_bit_decoder_7_display_1_b_2), .e(n4_bit_decoder_7_display_1_e), .d(n4_bit_decoder_7_display_1_d_2),
    .c(n4_bit_decoder_7_display_1_c_2));  // open: dp
  _7_Segment_Display u_7_segment_display_3 ();  // open: g, f, a, b, e, d, c, dp
  first_decoder first_decoder_2 (
    .C4(A_3[4]), .S3(A_3[3]), .S2(A_3[2]), .S1(A_3[1]), .S0(A_3[0]), .a(first_decoder_2_a),
    .b(first_decoder_2_b), .c(first_decoder_2_c), .d(first_decoder_2_d), .e(first_decoder_2_e),
    .f(first_decoder_2_f), .g(first_decoder_2_g));
  _7_Segment_Display u_7_segment_display_4 (
    .g(first_decoder_2_g), .f(first_decoder_2_f), .a(first_decoder_2_a), .b(first_decoder_2_b),
    .e(first_decoder_2_e), .d(first_decoder_2_d), .c(first_decoder_2_c));  // open: dp
  first_decoder first_decoder_3 (
    .C4(A[0]), .S3(A[1]), .S2(A[2]), .S1(A[3]), .S0(A[4]), .a(first_decoder_3_a), .b(first_decoder_3_b),
    .c(first_decoder_3_c), .d(first_decoder_3_d), .e(first_decoder_3_e), .f(first_decoder_3_f),
    .g(first_decoder_3_g));
  second_decoder second_decoder_1 (
    .C4(A_3[4]), .S3(A_3[3]), .S2(A_3[2]), .S1(A_3[1]), .S0(A_3[0]), .a(second_decoder_1_a),
    .b(second_decoder_1_b), .c(second_decoder_1_c), .d(second_decoder_1_d), .e(second_decoder_1_e),
    .f(second_decoder_1_f), .g(second_decoder_1_g));
  _7_Segment_Display u_7_segment_display_5 (
    .g(first_decoder_3_g), .f(first_decoder_3_f), .a(first_decoder_3_a), .b(first_decoder_3_b),
    .e(first_decoder_3_e), .d(first_decoder_3_d), .c(first_decoder_3_c));  // open: dp
  _7_Segment_Display u_7_segment_display_6 (
    .g(second_decoder_2_g), .f(second_decoder_2_f), .a(second_decoder_2_a), .b(second_decoder_2_b),
    .e(second_decoder_2_e), .d(second_decoder_2_d), .c(second_decoder_2_c));  // open: dp
  second_decoder second_decoder_2 (
    .C4(A[0]), .S3(A[1]), .S2(A[2]), .S1(A[3]), .S0(A[4]), .a(second_decoder_2_a), .b(second_decoder_2_b),
    .c(second_decoder_2_c), .d(second_decoder_2_d), .e(second_decoder_2_e), .f(second_decoder_2_f),
    .g(second_decoder_2_g));
  first_decoder first_decoder_4 (
    .C4(A_2[0]), .S3(A_2[1]), .S2(A_2[2]), .S1(A_2[3]), .S0(A_2[4]), .a(first_decoder_4_a),
    .b(first_decoder_4_b), .c(first_decoder_4_c), .d(first_decoder_4_d), .e(first_decoder_4_e),
    .f(first_decoder_4_f), .g(first_decoder_4_g));
  _7_Segment_Display u_7_segment_display_7 (
    .g(first_decoder_4_g), .f(first_decoder_4_f), .a(first_decoder_4_a), .b(first_decoder_4_b),
    .e(first_decoder_4_e), .d(first_decoder_4_d), .c(first_decoder_4_c));  // open: dp
  second_decoder second_decoder_3 (
    .C4(A_2[0]), .S3(A_2[1]), .S2(A_2[2]), .S1(A_2[3]), .S0(A_2[4]), .a(second_decoder_3_a),
    .b(second_decoder_3_b), .c(second_decoder_3_c), .d(second_decoder_3_d), .e(second_decoder_3_e),
    .f(second_decoder_3_f), .g(second_decoder_3_g));
  _7_Segment_Display u_7_segment_display_8 (
    .g(second_decoder_3_g), .f(second_decoder_3_f), .a(second_decoder_3_a), .b(second_decoder_3_b),
    .e(second_decoder_3_e), .d(second_decoder_3_d), .c(second_decoder_3_c));  // open: dp
endmodule

// Decoder1
module first_decoder (
  input  C4,
  input  S3,
  input  S2,
  input  S1,
  input  S0,
  output a,
  output b,
  output c,
  output d,
  output e,
  output f,
  output g
);

  wire and_1_out, and_2_out, and_3_out, and_4_out, and_5_out, and_6_out, and_7_out, and_8_out, and_9_out,
       and_10_out, and_11_out, and_12_out, and_13_out, and_14_out, and_15_out, and_16_out, and_17_out,
       and_18_out, and_19_out, and_20_out, and_21_out, and_22_out, and_23_out, and_24_out, and_25_out,
       and_26_out, and_27_out, and_28_out, and_29_out, and_30_out, and_31_out, and_32_out, and_33_out,
       and_34_out, and_35_out, and_36_out, and_37_out, and_38_out, and_39_out, and_40_out, and_41_out,
       and_42_out, and_43_out, and_44_out, and_45_out, and_46_out, and_47_out, and_48_out, and_49_out,
       and_50_out, and_51_out, and_52_out, and_53_out, and_54_out, and_55_out, and_56_out, not_1_out,
       not_2_out, not_3_out, not_4_out, not_5_out, not_6_out, not_7_out, not_8_out, not_9_out, not_10_out,
       not_11_out, not_12_out, not_13_out, not_14_out, not_15_out, not_16_out, not_17_out, not_18_out,
       not_19_out, not_20_out, not_21_out, not_22_out, not_23_out, not_24_out, not_25_out, not_26_out,
       not_27_out, not_28_out, not_29_out, not_30_out, not_31_out, not_32_out, not_33_out, not_34_out,
       not_35_out, not_36_out, not_37_out, not_38_out, not_39_out, not_40_out, not_41_out, not_42_out,
       not_43_out, not_44_out, not_45_out, not_46_out, not_47_out, not_48_out, not_49_out, not_50_out,
       not_51_out, not_52_out, not_53_out, not_54_out, not_55_out, not_56_out, not_57_out, not_58_out,
       not_59_out, not_60_out, not_61_out, not_62_out, not_63_out, not_64_out, not_65_out, not_66_out,
       not_67_out, not_68_out, not_69_out, not_70_out, not_71_out, not_72_out, not_73_out, not_74_out,
       not_75_out, not_76_out, not_77_out, not_78_out, not_79_out, not_80_out, not_81_out, not_82_out,
       not_83_out, not_84_out, not_85_out, not_86_out, not_87_out, not_88_out, not_89_out, not_90_out,
       not_91_out, not_92_out, not_93_out, not_94_out, not_95_out, not_96_out, not_97_out, not_98_out;

  not not_1 (not_1_out, C4);
  not not_2 (not_2_out, S2);
  not not_3 (not_3_out, S0);
  not not_4 (not_4_out, S3);
  not not_5 (not_5_out, C4);
  not not_6 (not_6_out, C4);
  not not_7 (not_7_out, S1);
  not not_8 (not_8_out, S1);
  not not_9 (not_9_out, S3);
  not not_10 (not_10_out, S0);
  not not_11 (not_11_out, S2);
  not not_12 (not_12_out, S0);
  not not_13 (not_13_out, C4);
  not not_14 (not_14_out, S2);
  not not_15 (not_15_out, C4);
  not not_16 (not_16_out, S1);
  not not_17 (not_17_out, S0);
  not not_18 (not_18_out, S3);
  not not_19 (not_19_out, S2);
  not not_20 (not_20_out, S3);
  not not_21 (not_21_out, S2);
  not not_22 (not_22_out, S3);
  not not_23 (not_23_out, S2);
  not not_24 (not_24_out, C4);
  not not_25 (not_25_out, S1);
  not not_26 (not_26_out, C4);
  not not_27 (not_27_out, S0);
  not not_28 (not_28_out, S1);
  not not_29 (not_29_out, S0);
  not not_30 (not_30_out, S3);
  not not_31 (not_31_out, S1);
  not not_32 (not_32_out, S2);
  not not_33 (not_33_out, S1);
  not not_34 (not_34_out, C4);
  not not_35 (not_35_out, S3);
  not not_36 (not_36_out, S2);
  not not_37 (not_37_out, S1);
  not not_38 (not_38_out, C4);
  not not_39 (not_39_out, S2);
  not not_40 (not_40_out, S0);
  not not_41 (not_41_out, S3);
  not not_42 (not_42_out, S2);
  not not_43 (not_43_out, S0);
  not not_44 (not_44_out, S3);
  not not_45 (not_45_out, S2);
  not not_46 (not_46_out, S3);
  not not_47 (not_47_out, S0);
  not not_48 (not_48_out, S2);
  not not_49 (not_49_out, S0);
  not not_50 (not_50_out, C4);
  not not_51 (not_51_out, S1);
  not not_52 (not_52_out, C4);
  not not_53 (not_53_out, S1);
  not not_54 (not_54_out, S1);
  not not_55 (not_55_out, C4);
  not not_56 (not_56_out, S3);
  not not_57 (not_57_out, S0);
  not not_58 (not_58_out, C4);
  not not_59 (not_59_out, S2);
  not not_60 (not_60_out, S0);
  not not_61 (not_61_out, S3);
  not not_62 (not_62_out, S2);
  not not_63 (not_63_out, S0);
  not not_64 (not_64_out, S3);
  not not_65 (not_65_out, S0);
  not not_66 (not_66_out, S2);
  not not_67 (not_67_out, S0);
  not not_68 (not_68_out, C4);
  not not_69 (not_69_out, S1);
  not not_70 (not_70_out, S0);
  not not_71 (not_71_out, S0);
  not not_72 (not_72_out, S3);
  not not_73 (not_73_out, S1);
  not not_74 (not_74_out, S0);
  not not_75 (not_75_out, C4);
  not not_76 (not_76_out, S3);
  not not_77 (not_77_out, S1);
  not not_78 (not_78_out, C4);
  not not_79 (not_79_out, S3);
  not not_80 (not_80_out, S0);
  not not_81 (not_81_out, S2);
  not not_82 (not_82_out, S1);
  not not_83 (not_83_out, S0);
  not not_84 (not_84_out, C4);
  not not_85 (not_85_out, S3);
  not not_86 (not_86_out, S2);
  not not_87 (not_87_out, S1);
  not not_88 (not_88_out, S3);
  not not_89 (not_89_out, S2);
  not not_90 (not_90_out, S3);
  not not_91 (not_91_out, S0);
  not not_92 (not_92_out, C4);
  not not_93 (not_93_out, S1);
  not not_94 (not_94_out, S1);
  not not_95 (not_95_out, C4);
  not not_96 (not_96_out, S2);
  not not_97 (not_97_out, S0);
  not not_98 (not_98_out, S3);
  and and_1 (and_1_out, not_1_out, not_2_out, not_3_out);
  and and_2 (and_2_out, not_4_out, S1);
  and and_3 (and_3_out, not_5_out, S2, S0);
  and and_4 (and_4_out, not_6_out, S3, not_7_out);
  and and_5 (and_5_out, S3, S2, not_8_out);
  and and_6 (and_6_out, C4, not_9_out, not_10_out);
  and and_7 (and_7_out, C4, not_11_out, S0);
  and and_8 (and_8_out, C4, S1, not_12_out);
  and and_9 (and_9_out, not_13_out, not_14_out);
  and and_10 (and_10_out, not_15_out, not_16_out, not_17_out);
  and and_11 (and_11_out, not_18_out, not_19_out, S0);
  and and_12 (and_12_out, not_20_out, not_21_out, S1);
  and and_13 (and_13_out, not_22_out, S1, S0);
  and and_14 (and_14_out, not_23_out, S1, S0);
  and and_15 (and_15_out, not_24_out, S3, not_25_out);
  and and_16 (and_16_out, not_26_out, S3, not_27_out);
  and and_17 (and_17_out, S3, not_28_out, not_29_out);
  and and_18 (and_18_out, C4, S2);
  and and_19 (and_19_out, not_30_out, not_31_out);
  and and_20 (and_20_out, not_32_out, not_33_out);
  and and_21 (and_21_out, not_34_out, not_35_out, S2);
  and and_22 (and_22_out, S3, S1);
  and and_23 (and_23_out, C4, not_36_out);
  and and_24 (and_24_out, C4, not_37_out);
  and and_25 (and_25_out, not_38_out, not_39_out, not_40_out);
  and and_26 (and_26_out, not_41_out, not_42_out, not_43_out);
  and and_27 (and_27_out, not_44_out, not_45_out, S1);
  and and_28 (and_28_out, not_46_out, S1, not_47_out);
  and and_29 (and_29_out, not_48_out, S1, not_49_out);
  and and_30 (and_30_out, not_50_out, S2, not_51_out, S0);
  and and_31 (and_31_out, not_52_out, S3, not_53_out);
  and and_32 (and_32_out, S3, not_54_out, S0);
  and and_33 (and_33_out, not_55_out, S3, S2, S0);
  and and_34 (and_34_out, C4, not_56_out, S1);
  and and_35 (and_35_out, C4, S2, not_57_out);
  and and_36 (and_36_out, not_58_out, not_59_out, not_60_out);
  and and_37 (and_37_out, not_61_out, not_62_out, not_63_out);
  and and_38 (and_38_out, not_64_out, S1, not_65_out);
  and and_39 (and_39_out, not_66_out, S1, not_67_out);
  and and_40 (and_40_out, not_68_out, S3, not_69_out, not_70_out);
  and and_41 (and_41_out, C4, S2, not_71_out);
  and and_42 (and_42_out, not_72_out, not_73_out, not_74_out);
  and and_43 (and_43_out, not_75_out, not_76_out, S2, not_77_out);
  and and_44 (and_44_out, not_78_out, not_79_out, S2, not_80_out);
  and and_45 (and_45_out, S3, not_81_out, not_82_out);
  and and_46 (and_46_out, S3, S1, not_83_out);
  and and_47 (and_47_out, not_84_out, S3, S2, S1);
  and and_48 (and_48_out, C4, not_85_out, not_86_out, S1);
  and and_49 (and_49_out, C4, S3, not_87_out);
  and and_50 (and_50_out, not_88_out, not_89_out, S1);
  and and_51 (and_51_out, not_90_out, S1, not_91_out);
  and and_52 (and_52_out, not_92_out, S2, not_93_out);
  and and_53 (and_53_out, S3, not_94_out);
  and and_54 (and_54_out, not_95_out, S3, S2);
  and and_55 (and_55_out, C4, not_96_out, not_97_out);
  and and_56 (and_56_out, C4, not_98_out, S1);
  or or_1 (a, and_1_out, and_2_out, and_3_out, and_4_out, and_5_out, and_6_out, and_7_out, and_8_out);
  or or_2 (b, and_9_out, and_10_out, and_11_out, and_12_out, and_13_out, and_14_out, and_15_out, and_16_out, and_17_out, and_18_out);
  or or_3 (c, and_19_out, and_20_out, S0, and_21_out, and_22_out, and_23_out, and_24_out);
  or or_4 (d, and_25_out, and_26_out, and_27_out, and_28_out, and_29_out, and_30_out, and_31_out, and_32_out, and_33_out, and_34_out, and_35_out);
  or or_5 (e, and_36_out, and_37_out, and_38_out, and_39_out, and_40_out, and_41_out);
  or or_6 (f, and_42_out, and_43_out, and_44_out, and_45_out, and_46_out, and_47_out, and_48_out, and_49_out);
  or or_7 (g, and_50_out, and_51_out, and_52_out, and_53_out, and_54_out, and_55_out, and_56_out);
endmodule

// Decoder2
module second_decoder (
  input  C4,
  input  S3,
  input  S2,
  input  S1,
  input  S0,
  output a,
  output b,
  output c,
  output d,
  output e,
  output f,
  output g
);

  wire and_1_out, and_2_out, and_3_out, and_4_out, and_5_out, and_6_out, and_7_out, and_8_out, and_9_out,
       and_10_out, and_11_out, and_12_out, and_13_out, and_14_out, and_15_out, and_16_out, and_17_out,
       and_18_out, and_19_out, not_1_out, not_2_out, not_3_out, not_4_out, not_5_out, not_6_out, not_7_out,
       not_8_out, not_9_out, not_10_out, not_11_out, not_12_out, not_13_out, not_14_out, not_15_out,
       not_16_out, not_17_out, not_18_out, not_19_out, not_20_out, not_21_out, not_22_out, not_23_out,
       not_24_out, not_25_out, not_26_out, not_27_out, not_28_out;

  not not_1 (not_1_out, C4);
  not not_2 (not_2_out, S3);
  not not_3 (not_3_out, C4);
  not not_4 (not_4_out, S2);
  not not_5 (not_5_out, S1);
  not not_6 (not_6_out, S3);
  not not_7 (not_7_out, S3);
  not not_8 (not_8_out, S2);
  not not_9 (not_9_out, C4);
  not not_10 (not_10_out, S3);
  not not_11 (not_11_out, C4);
  not not_12 (not_12_out, S2);
  not not_13 (not_13_out, S1);
  not not_14 (not_14_out, S3);
  not not_15 (not_15_out, C4);
  not not_16 (not_16_out, S3);
  not not_17 (not_17_out, C4);
  not not_18 (not_18_out, S2);
  not not_19 (not_19_out, S1);
  not not_20 (not_20_out, S3);
  not not_21 (not_21_out, S2);
  not not_22 (not_22_out, S1);
  not not_23 (not_23_out, C4);
  not not_24 (not_24_out, S3);
  not not_25 (not_25_out, C4);
  not not_26 (not_26_out, S2);
  not not_27 (not_27_out, S1);
  and and_1 (and_1_out, C4, S2);
  and and_2 (and_2_out, C4, S3);
  and and_3 (and_3_out, not_1_out, not_2_out);
  and and_4 (and_4_out, not_3_out, not_4_out, not_5_out);
  and and_5 (and_5_out, not_6_out, S2);
  and and_6 (and_6_out, C4, S3);
  not not_28 (not_28_out, C4);
  and and_7 (and_7_out, not_7_out, not_8_out);
  and and_8 (and_8_out, S3, S2, S1);
  and and_9 (and_9_out, not_9_out, not_10_out);
  and and_10 (and_10_out, not_11_out, not_12_out, not_13_out);
  and and_11 (and_11_out, not_14_out, S2);
  and and_12 (and_12_out, C4, S3);
  and and_13 (and_13_out, not_15_out, not_16_out);
  and and_14 (and_14_out, not_17_out, not_18_out, not_19_out);
  and and_15 (and_15_out, not_20_out, S2);
  and and_16 (and_16_out, C4, S3, not_21_out);
  and and_17 (and_17_out, C4, S3, not_22_out);
  and and_18 (and_18_out, not_23_out, not_24_out);
  and and_19 (and_19_out, not_25_out, not_26_out, not_27_out);
  or or_1 (g, and_1_out, and_2_out);
  or or_2 (a, and_3_out, and_4_out, and_5_out, and_6_out);
  or or_3 (c, not_28_out, and_7_out, and_8_out);
  or or_4 (d, and_9_out, and_10_out, and_11_out, and_12_out);
  or or_5 (e, and_13_out, and_14_out, and_15_out, and_16_out, and_17_out);
  or or_6 (f, and_18_out, and_19_out);

  assign b = 1'b1;
endmodule

module displayV1 (
  input  [4:0] A,
  input  in_2,
  input  [4:0] B,
  input  in_4
);

  wire first_decoder_1_a, first_decoder_1_b, first_decoder_1_c, first_decoder_1_d, first_decoder_1_e,
       first_decoder_1_f, first_decoder_1_g, not_1_out, second_decoder_1_a, second_decoder_1_b,
       second_decoder_1_c, second_decoder_1_d, second_decoder_1_e, second_decoder_1_f, second_decoder_1_g,
       subormult_1_c;
  wire [4:0] multiplexer_1_out, n2_s_compliment_1_out, subormult_1_s0;

  SubOrMult subormult_1 (
    .B4(B[4]), .A4(A[4]), .B3(B[3]), .A3(A[3]), .B2(B[2]), .A2(A[2]), .B1(B[1]), .A1(A[1]), .B0(B[0]),
    .A0(A[0]), .C(subormult_1_c), .S4(subormult_1_s0[4]), .S3(subormult_1_s0[3]), .S2(subormult_1_s0[2]),
    .S1(subormult_1_s0[1]), .S0(subormult_1_s0[0]), .M(in_2));  // open: V
  _2_s_Compliment u_2_s_compliment_1 (
    .S0(subormult_1_s0[0]), .S1(subormult_1_s0[1]), .S2(subormult_1_s0[2]), .S3(subormult_1_s0[3]),
    .S4(subormult_1_s0[4]), ._111(in_4), .Out(n2_s_compliment_1_out));
  Multiplexer #(.width(5)) multiplexer_1 (
    .in0(n2_s_compliment_1_out), .in1(subormult_1_s0), .out(multiplexer_1_out), .sel(subormult_1_c));  // open: en
  first_decoder first_decoder_1 (
    .C4(multiplexer_1_out[4]), .S3(multiplexer_1_out[3]), .S2(multiplexer_1_out[2]),
    .S1(multiplexer_1_out[1]), .S0(multiplexer_1_out[0]), .a(first_decoder_1_a), .b(first_decoder_1_b),
    .c(first_decoder_1_c), .d(first_decoder_1_d), .e(first_decoder_1_e), .f(first_decoder_1_f),
    .g(first_decoder_1_g));
  not not_1 (not_1_out, subormult_1_c);
  _7_Segment_Display u_7_segment_display_1 (
    .g(first_decoder_1_g), .f(first_decoder_1_f), .a(first_decoder_1_a), .b(first_decoder_1_b),
    .e(first_decoder_1_e), .d(first_decoder_1_d), .c(first_decoder_1_c));  // open: dp
  _7_Segment_Display u_7_segment_display_2 (.g(not_1_out));  // open: f, a, b, e, d, c, dp
  _7_Segment_Display u_7_segment_display_3 (
    .g(second_decoder_1_g), .f(second_decoder_1_f), .a(second_decoder_1_a), .b(second_decoder_1_b),
    .e(second_decoder_1_e), .d(second_decoder_1_d), .c(second_decoder_1_c));  // open: dp
  second_decoder second_decoder_1 (
    .C4(multiplexer_1_out[4]), .S3(multiplexer_1_out[3]), .S2(multiplexer_1_out[2]),
    .S1(multiplexer_1_out[1]), .S0(multiplexer_1_out[0]), .a(second_decoder_1_a), .b(second_decoder_1_b),
    .c(second_decoder_1_c), .d(second_decoder_1_d), .e(second_decoder_1_e), .f(second_decoder_1_f),
    .g(second_decoder_1_g));
endmodule

// Sub
module sub (
  input  [4:0] A,
  input  in_2,
  input  [4:0] B,
  input  in_4,
  output minus,
  output a1,
  output b1,
  output a2,
  output b2,
  output a3,
  output b3,
  output a4,
  output b4,
  output a5,
  output b5,
  output a6,
  output b6,
  output a7,
  output b7,
  output [4:0] Hex
);

  wire subormult_1_c;
  wire [4:0] n2_s_compliment_1_out, subormult_1_s0;

  SubOrMult subormult_1 (
    .B4(B[4]), .A4(A[4]), .B3(B[3]), .A3(A[3]), .B2(B[2]), .A2(A[2]), .B1(B[1]), .A1(A[1]), .B0(B[0]),
    .A0(A[0]), .C(subormult_1_c), .S4(subormult_1_s0[4]), .S3(subormult_1_s0[3]), .S2(subormult_1_s0[2]),
    .S1(subormult_1_s0[1]), .S0(subormult_1_s0[0]), .M(in_2));  // open: V
  _2_s_Compliment u_2_s_compliment_1 (
    .S0(subormult_1_s0[0]), .S1(subormult_1_s0[1]), .S2(subormult_1_s0[2]), .S3(subormult_1_s0[3]),
    .S4(subormult_1_s0[4]), ._111(in_4), .Out(n2_s_compliment_1_out));
  Multiplexer #(.width(5)) multiplexer_1 (
    .in0(n2_s_compliment_1_out), .in1(subormult_1_s0), .out({Hex[0], Hex[1], Hex[2], Hex[3], Hex[4]}),
    .sel(subormult_1_c));  // open: en
  first_decoder first_decoder_1 (
    .C4(Hex[0]), .S3(Hex[1]), .S2(Hex[2]), .S1(Hex[3]), .S0(Hex[4]), .a(a1), .b(a2), .c(a3), .d(a4), .e(a5),
    .f(a6), .g(a7));
  not not_1 (minus, subormult_1_c);
  second_decoder second_decoder_1 (
    .C4(Hex[0]), .S3(Hex[1]), .S2(Hex[2]), .S1(Hex[3]), .S0(Hex[4]), .a(b1), .b(b2), .c(b3), .d(b4), .e(b5),
    .f(b6), .g(b7));
endmodule

module final_layout (
  input  [4:0] in_1,
  input  [4:0] B,
  input  in_3,
  input  in_4
);

  wire first_decoder_1_a, first_decoder_1_b, first_decoder_1_c, first_decoder_1_d, first_decoder_1_e,
       first_decoder_1_f, first_decoder_1_g, first_decoder_2_a, first_decoder_2_b, first_decoder_2_c,
       first_decoder_2_d, first_decoder_2_e, first_decoder_2_f, first_decoder_2_g, second_decoder_1_a,
       second_decoder_1_b, second_decoder_1_c, second_decoder_1_d, second_decoder_1_e, second_decoder_1_f,
       second_decoder_1_g, second_decoder_2_a, second_decoder_2_b, second_decoder_2_c, second_decoder_2_d,
       second_decoder_2_e, second_decoder_2_f, second_decoder_2_g, sub_1_a1, sub_1_a2, sub_1_a3, sub_1_a4,
       sub_1_a5, sub_1_a6, sub_1_a7, sub_1_b1, sub_1_b2, sub_1_b3, sub_1_b4, sub_1_b5, sub_1_b6, sub_1_b7,
       sub_1_minus;
  wire [3:0] n1dh_1_a, n1dh_2_a, n1dh_3_a, n2dh_1_a, n2dh_2_a, n2dh_3_a;
  wire [4:0] sub_1_hex;

  _7_Segment_Display u_7_segment_display_1 (
    .g(first_decoder_1_g), .f(first_decoder_1_f), .a(first_decoder_1_a), .b(first_decoder_1_b),
    .e(first_decoder_1_e), .d(first_decoder_1_d), .c(first_decoder_1_c));  // open: dp
  _7_Segment_Display u_7_segment_display_2 (
    .g(second_decoder_1_g), .f(second_decoder_1_f), .a(second_decoder_1_a), .b(second_decoder_1_b),
    .e(second_decoder_1_e), .d(second_decoder_1_d), .c(second_decoder_1_c));  // open: dp
  first_decoder first_decoder_1 (
    .C4(in_1[4]), .S3(in_1[3]), .S2(in_1[2]), .S1(in_1[1]), .S0(in_1[0]), .a(first_decoder_1_a),
    .b(first_decoder_1_b), .c(first_decoder_1_c), .d(first_decoder_1_d), .e(first_decoder_1_e),
    .f(first_decoder_1_f), .g(first_decoder_1_g));
  _7_Segment_Display u_7_segment_display_3 (
    .g(second_decoder_2_g), .f(second_decoder_2_f), .a(second_decoder_2_a), .b(second_decoder_2_b),
    .e(second_decoder_2_e), .d(second_decoder_2_d), .c(second_decoder_2_c));  // open: dp
  _7_Segment_Display u_7_segment_display_4 (
    .g(first_decoder_2_g), .f(first_decoder_2_f), .a(first_decoder_2_a), .b(first_decoder_2_b),
    .e(first_decoder_2_e), .d(first_decoder_2_d), .c(first_decoder_2_c));  // open: dp
  first_decoder first_decoder_2 (
    .C4(B[4]), .S3(B[3]), .S2(B[2]), .S1(B[1]), .S0(B[0]), .a(first_decoder_2_a), .b(first_decoder_2_b),
    .c(first_decoder_2_c), .d(first_decoder_2_d), .e(first_decoder_2_e), .f(first_decoder_2_f),
    .g(first_decoder_2_g));
  second_decoder second_decoder_1 (
    .C4(in_1[4]), .S3(in_1[3]), .S2(in_1[2]), .S1(in_1[1]), .S0(in_1[0]), .a(second_decoder_1_a),
    .b(second_decoder_1_b), .c(second_decoder_1_c), .d(second_decoder_1_d), .e(second_decoder_1_e),
    .f(second_decoder_1_f), .g(second_decoder_1_g));
  second_decoder second_decoder_2 (
    .C4(B[4]), .S3(B[3]), .S2(B[2]), .S1(B[1]), .S0(B[0]), .a(second_decoder_2_a), .b(second_decoder_2_b),
    .c(second_decoder_2_c), .d(second_decoder_2_d), .e(second_decoder_2_e), .f(second_decoder_2_f),
    .g(second_decoder_2_g));
  _7_Segment_Display u_7_segment_display_5 (.g(sub_1_minus));  // open: f, a, b, e, d, c, dp
  _7_Segment_Display u_7_segment_display_6 (
    .g(sub_1_b7), .f(sub_1_b6), .a(sub_1_b1), .b(sub_1_b2), .e(sub_1_b5), .d(sub_1_b4), .c(sub_1_b3));  // open: dp
  _7_Segment_Display u_7_segment_display_7 (
    .g(sub_1_a7), .f(sub_1_a6), .a(sub_1_a1), .b(sub_1_a2), .e(sub_1_a5), .d(sub_1_a4), .c(sub_1_a3));  // open: dp
  Hex_Digit_Display hex_digit_display_1 (.value(n2dh_1_a));  // open: dp
  _2dH u_2dh_1 (
    .C4(in_1[4]), .S3(in_1[3]), .S2(in_1[2]), .S1(in_1[1]), .S0(in_1[0]), .a(n2dh_1_a[0]), .b(n2dh_1_a[1]),
    .c(n2dh_1_a[2]), .d(n2dh_1_a[3]));
  Hex_Digit_Display hex_digit_display_2 (.value(n1dh_1_a));  // open: dp
  _1dH u_1dh_1 (
    .C4(in_1[4]), .S3(in_1[3]), .S2(in_1[2]), .S1(in_1[1]), .S0(in_1[0]), .a(n1dh_1_a[0]), .b(n1dh_1_a[1]),
    .c(n1dh_1_a[2]), .d(n1dh_1_a[3]));
  sub sub_1 (
    .A(in_1), .B(B), .in_4(in_3), .Hex(sub_1_hex), .in_2(in_4), .minus(sub_1_minus), .a1(sub_1_a1),
    .b1(sub_1_b1), .a2(sub_1_a2), .b2(sub_1_b2), .a3(sub_1_a3), .b3(sub_1_b3), .a4(sub_1_a4), .b4(sub_1_b4),
    .a5(sub_1_a5), .b5(sub_1_b5), .a6(sub_1_a6), .b6(sub_1_b6), .a7(sub_1_a7), .b7(sub_1_b7));
  Hex_Digit_Display hex_digit_display_3 (.value(n2dh_2_a));  // open: dp
  _2dH u_2dh_2 (
    .C4(B[4]), .S3(B[3]), .S2(B[2]), .S1(B[1]), .S0(B[0]), .a(n2dh_2_a[0]), .b(n2dh_2_a[1]), .c(n2dh_2_a[2]),
    .d(n2dh_2_a[3]));
  _1dH u_1dh_2 (
    .C4(B[4]), .S3(B[3]), .S2(B[2]), .S1(B[1]), .S0(B[0]), .a(n1dh_2_a[0]), .b(n1dh_2_a[1]), .c(n1dh_2_a[2]),
    .d(n1dh_2_a[3]));
  Hex_Digit_Display hex_digit_display_4 (.value(n1dh_2_a));  // open: dp
  _7_Segment_Display u_7_segment_display_8 (.g(sub_1_minus));  // open: f, a, b, e, d, c, dp
  _2dH u_2dh_3 (
    .C4(sub_1_hex[0]), .S3(sub_1_hex[1]), .S2(sub_1_hex[2]), .S1(sub_1_hex[3]), .S0(sub_1_hex[4]),
    .a(n2dh_3_a[0]), .b(n2dh_3_a[1]), .c(n2dh_3_a[2]), .d(n2dh_3_a[3]));
  Hex_Digit_Display hex_digit_display_5 (.value(n2dh_3_a));  // open: dp
  _1dH u_1dh_3 (
    .C4(sub_1_hex[0]), .S3(sub_1_hex[1]), .S2(sub_1_hex[2]), .S1(sub_1_hex[3]), .S0(sub_1_hex[4]),
    .a(n1dh_3_a[0]), .b(n1dh_3_a[1]), .c(n1dh_3_a[2]), .d(n1dh_3_a[3]));
  Hex_Digit_Display hex_digit_display_6 (.value(n1dh_3_a));  // open: dp

  // Notes on the sheet:
  //   A
  //   -
  //   =
  //   -
  //   =
endmodule

module _1dH (
  input  C4,
  input  S3,
  input  S2,
  input  S1,
  input  S0,
  output a,
  output b,
  output c,
  output d
);


  assign a = S0;
  assign b = S1;
  assign c = S2;
  assign d = S3;
endmodule

module _2dH (
  input  C4,
  input  S3,
  input  S2,
  input  S1,
  input  S0,
  output a,
  output b,
  output c,
  output d
);


  assign a = C4;
  assign b = 1'b0;
  assign c = 1'b0;
  assign d = 1'b0;
endmodule
